// Logisim project Fcpu copy.circ as structural Verilog
module multiplexor (
  input  A,
  input  B,
  input  Selection,
  output Output
);

  wire And_2_out, And_out, Not_out;

  not Not (Not_out, Selection);
  and And (And_out, B, Selection);
  and And_2 (And_2_out, A, Not_out);
  or Or (Output, And_out, And_2_out);
endmodule

// SR
module SR_Latch (
  input  Reset,
  input  Set,
  output Q,
  output Q_Not
);

  wire or_1_out, or_2_out;

  or or_1 (or_1_out, Reset, Q_Not);
  or or_2 (or_2_out, Q, Set);
  not not_1 (Q, or_1_out);
  not not_2 (Q_Not, or_2_out);

  // Notes on the sheet:
  //   SR Latch
  //   Cuando activo Set, se guarda 1 en Q
  //   Cuando activo Reset, se guarda 0 en Q
endmodule

// D L
module D_Latch (
  input  Clock,
  input  Data,
  output Q,
  output Q_Not
);

  wire and_1_out, and_2_out, not_1_out;

  not not_1 (not_1_out, Data);
  and and_1 (and_1_out, Clock, not_1_out);
  and and_2 (and_2_out, Data, Clock);
  SR_Latch sr_latch_1 (.Reset(and_1_out), .Set(and_2_out), .Q(Q), .Q_Not(Q_Not));

  // Notes on the sheet:
  //   D Latch
  //   Cuando Activo el Clock, se guarda en Q los que tenga Data
endmodule

module D_Flip_Flop (
  input  Data,
  input  Clock,
  output Q,
  output Q_Not
);

  wire d_latch_1_q, not_1_out;

  D_Latch d_latch_1 (.Clock(Clock), .Data(Data), .Q(d_latch_1_q));  // open: Q_Not
  not not_1 (not_1_out, Clock);
  D_Latch d_latch_2 (.Clock(not_1_out), .Data(d_latch_1_q), .Q(Q), .Q_Not(Q_Not));

  // Notes on the sheet:
  //   Cuando el Clock se activa no pasa nada, 
  //   D Flip-Flop
  //   pero cuando el Clock baja guarda en Q lo que hay en Data
endmodule

module Dec_2x4 (
  input  A,
  input  B,
  output _0,
  output _1,
  output out_5,
  output out_6
);

  wire not_1_out, not_2_out, not_3_out, not_4_out;

  not not_1 (not_1_out, A);
  not not_2 (not_2_out, B);
  not not_3 (not_3_out, B);
  not not_4 (not_4_out, A);
  and and_1 (_0, not_1_out, not_2_out);
  and and_2 (_1, A, not_3_out);
  and and_3 (out_5, not_4_out, B);
  and and_4 (out_6, B, A);
endmodule

module Dec_3x8 (
  input  a2,
  input  b1,
  input  c0,
  input  Enable,
  output x7,
  output y6,
  output z5,
  output u4,
  output v3,
  output w2,
  output s1,
  output t0
);

  wire not_1_out, not_2_out, not_3_out, not_4_out, not_5_out, not_6_out, not_7_out, not_8_out, not_9_out,
       not_10_out, not_11_out, not_12_out;

  and and_1 (x7, a2, b1, c0);
  not not_1 (not_1_out, c0);
  not not_2 (not_2_out, b1);
  not not_3 (not_3_out, b1);
  not not_4 (not_4_out, c0);
  not not_5 (not_5_out, a2);
  not not_6 (not_6_out, a2);
  not not_7 (not_7_out, c0);
  not not_8 (not_8_out, a2);
  not not_9 (not_9_out, b1);
  not not_10 (not_10_out, a2);
  not not_11 (not_11_out, b1);
  not not_12 (not_12_out, c0);
  and and_2 (y6, a2, b1, not_1_out);
  and and_3 (z5, a2, not_2_out, c0);
  and and_4 (u4, a2, not_3_out, not_4_out);
  and and_5 (v3, not_5_out, b1, c0);
  and and_6 (w2, not_6_out, b1, not_7_out);
  and and_7 (s1, not_8_out, not_9_out, c0);
  and and_8 (t0, not_10_out, not_11_out, not_12_out);
endmodule

module _16Bits_CPU (
  input  Clear,
  output [12:0] Control_Output,
  output [15:0] Output__Normal
);

  wire and_1_out, Clock_out, n16bits_alu_1_p5, not_1_out;
  wire [15:0] adder_1_out, adder_2_out, bit_extender_1_out, bit_extender_2_out, bit_extender_3_out, Data_in,
       main_1_p2, main_1_p7, main_1_p8, multiplexer_1_out, multiplexer_2_out, multiplexer_3_out,
       multiplexer_5_out, n16bits_alu_1_p4, PC_q, ram_2_data;

  Clock Clock (.out(Clock_out));
  Register #(.width(16)) PC (.D(multiplexer_5_out), .en(Clock_out), .Q(PC_q), .clk(Clock_out), .clr(Clear));
  Adder #(.width(16)) adder_1 (.a(PC_q), .b(16'h1), .out(adder_1_out));  // open: cin, cout
  Adder #(.width(16)) adder_2 (.a(PC_q), .b(bit_extender_1_out), .out(adder_2_out));  // open: cin, cout
  RAM #(.addrWidth(16), .dataWidth(16)) ram_1 (.addr(PC_q), .data(Output__Normal), .clr(Clear));  // open: sel, clk, ld
  assign bit_extender_1_out = {{8{Output__Normal[7]}}, Output__Normal[7:0]};  // Bit_Extender bit_extender_1
  // Register_File_main main_1: pin names not known; wires that end beside it: Clock_out, main_1_p2, Output__Normal[7:4], Output__Normal[3:0], Output__Normal[11:8], Control_Output[3], main_1_p7, main_1_p8, Data_in
  assign bit_extender_2_out = {{8{Output__Normal[7]}}, Output__Normal[7:0]};  // Bit_Extender bit_extender_2
  Multiplexer #(.width(16), .disabled(0), .enable("false")) multiplexer_1 (
    .in0(adder_1_out), .in1(adder_2_out), .out(multiplexer_1_out), .sel(and_1_out));
  and and_1 (and_1_out, not_1_out, Control_Output[10]);
  Multiplexer #(.width(16), .disabled(0), .enable("false")) multiplexer_2 (
    .in0(main_1_p7), .in1(Data_in), .out(multiplexer_2_out), .sel(Control_Output[12]));
  Multiplexer #(.select(3), .width(16), .disabled(0), .enable("false")) multiplexer_3 (
    .in0({16{1'b0}}), .in1(main_1_p7), .in2(main_1_p8), .in3(Data_in), .in4(bit_extender_2_out),
    .out(multiplexer_3_out), .sel(Control_Output[6:4]));  // open: in5, in6, in7
  assign bit_extender_3_out = {{4{Output__Normal[11]}}, Output__Normal[11:0]};  // Bit_Extender bit_extender_3
  not not_1 (not_1_out, n16bits_alu_1_p5);
  Multiplexer #(.width(16), .disabled(0), .enable("false")) multiplexer_4 (
    .in0(n16bits_alu_1_p4), .in1(ram_2_data), .out(main_1_p2), .sel(Control_Output[8]));
  // _16bits_ALU 16bits_alu_1: pin names not known; wires that end beside it: multiplexer_2_out, multiplexer_3_out, Control_Output[2:0], n16bits_alu_1_p4, n16bits_alu_1_p5
  Multiplexer #(.width(16), .disabled(0), .enable("false")) multiplexer_5 (
    .in0(multiplexer_1_out), .in1(bit_extender_3_out), .out(multiplexer_5_out), .sel(Control_Output[11]));
  ROM #(.addrWidth(4), .dataWidth(13)) rom_1 (.addr(Output__Normal[15:12]), .data(Control_Output));  // open: sel
  RAM #(.addrWidth(16), .dataWidth(16), .bus("separate")) ram_2 (
    .addr(n16bits_alu_1_p4), .din(Data_in), .data(ram_2_data), .str(Control_Output[7]), .clk(Clock_out),
    .ld(Control_Output[9]));  // open: sel, clr

  // Other names for the same wires on the sheet: ALU_Control[2:0] = Control_Output[2:0]; RegWrite = Control_Output[3];
  //   ALU_Src[2:0] = Control_Output[6:4]; MemWrite = Control_Output[7]; MemtoReq = Control_Output[8];
  //   MemRead = Control_Output[9]; RegDest = Control_Output[12]

  // Notes on the sheet:
  //   16-bit CPU
  //   Instruction Memory
  //   Branch
  //   Zero
  //   Jump
  //   Branch
  //   Data Memory
  //   December 2014
  //   Control
  //   contents of rom_1 (hex, n*v repeats v):
  //   2a 2e 32a a2 28 29 2b 0 104a 0 1442 1442 0 0 0 842
  //   Bianca I. Colón Rosado
  //   CCOM4086 Computer Architecture
endmodule
