// Logisim project Register File copy.circ as structural Verilog: 2 circuits, main circuit main
module main (
  input  Clock,
  input  [15:0] DATA,
  input  Enable,
  input  [3:0] RS,
  input  [3:0] RT,
  input  [3:0] RD,
  output [15:0] Outpot_RS,
  output [15:0] Output_RT,
  output [15:0] Output_RD
);

  wire decoder_1_out0, decoder_1_out1, decoder_1_out2, decoder_1_out3, decoder_1_out4, decoder_1_out5,
       decoder_1_out6, decoder_1_out7, decoder_1_out8, decoder_1_out9, decoder_1_out10, decoder_1_out11,
       decoder_1_out12, decoder_1_out13, decoder_1_out14, decoder_1_out15;
  wire [15:0] _0_q, _1_q, _2_q, _3_q, _4_q, _5_q, _6_q, _7_q, _8_q, _9_q, _10_q, _11_q, _12_q, _13_q, _14_q,
       _15_q;

  Decoder #(.select(4), .disabled(0)) decoder_1 (
    .out0(decoder_1_out0), .out1(decoder_1_out1), .out2(decoder_1_out2), .out3(decoder_1_out3),
    .out4(decoder_1_out4), .out5(decoder_1_out5), .out6(decoder_1_out6), .out7(decoder_1_out7),
    .out8(decoder_1_out8), .out9(decoder_1_out9), .out10(decoder_1_out10), .out11(decoder_1_out11),
    .out12(decoder_1_out12), .out13(decoder_1_out13), .out14(decoder_1_out14), .out15(decoder_1_out15),
    .sel(RD), .en(Enable));
  Register #(.width(16)) _0 (.D(DATA), .en(decoder_1_out0), .Q(_0_q), .clk(Clock));  // open: clr
  Register #(.width(16)) _1 (.D(DATA), .en(decoder_1_out1), .Q(_1_q), .clk(Clock));  // open: clr
  Register #(.width(16)) _2 (.D(DATA), .en(decoder_1_out2), .Q(_2_q), .clk(Clock));  // open: clr
  Register #(.width(16)) _3 (.D(DATA), .en(decoder_1_out3), .Q(_3_q), .clk(Clock));  // open: clr
  Register #(.width(16)) _4 (.D(DATA), .en(decoder_1_out4), .Q(_4_q), .clk(Clock));  // open: clr
  Register #(.width(16)) _5 (.D(DATA), .en(decoder_1_out5), .Q(_5_q), .clk(Clock));  // open: clr
  Register #(.width(16)) _6 (.D(DATA), .en(decoder_1_out6), .Q(_6_q), .clk(Clock));  // open: clr
  Register #(.width(16)) _7 (.D(DATA), .en(decoder_1_out7), .Q(_7_q), .clk(Clock));  // open: clr
  Register #(.width(16)) _8 (.D(DATA), .en(decoder_1_out8), .Q(_8_q), .clk(Clock));  // open: clr
  Register #(.width(16)) _9 (.D(DATA), .en(decoder_1_out9), .Q(_9_q), .clk(Clock));  // open: clr
  Register #(.width(16)) _10 (.D(DATA), .en(decoder_1_out10), .Q(_10_q), .clk(Clock));  // open: clr
  Register #(.width(16)) _11 (.D(DATA), .en(decoder_1_out11), .Q(_11_q), .clk(Clock));  // open: clr
  Register #(.width(16)) _12 (.D(DATA), .en(decoder_1_out12), .Q(_12_q), .clk(Clock));  // open: clr
  Register #(.width(16)) _13 (.D(DATA), .en(decoder_1_out13), .Q(_13_q), .clk(Clock));  // open: clr
  Register #(.width(16)) _14 (.D(DATA), .en(decoder_1_out14), .Q(_14_q), .clk(Clock));  // open: clr
  Register #(.width(16)) _15 (.D(DATA), .en(decoder_1_out15), .Q(_15_q), .clk(Clock));  // open: clr
  Multiplexer #(.select(4), .width(16), .enable("false")) multiplexer_1 (
    .in0(_0_q), .in1(_1_q), .in2(_2_q), .in3(_3_q), .in4(_4_q), .in5(_5_q), .in6(_6_q), .in7(_7_q),
    .in8(_8_q), .in9(_9_q), .in10(_10_q), .in11(_11_q), .in12(_12_q), .in13(_13_q), .in14(_14_q),
    .in15(_15_q), .out(Outpot_RS), .sel(RS));
  Multiplexer #(.select(4), .width(16)) multiplexer_2 (
    .in0(_0_q), .in1(_1_q), .in2(_2_q), .in3(_3_q), .in4(_4_q), .in5(_5_q), .in6(_6_q), .in7(_7_q),
    .in8(_8_q), .in9(_9_q), .in10(_10_q), .in11(_11_q), .in12(_12_q), .in13(_13_q), .in14(_14_q),
    .in15(_15_q), .out(Output_RT), .sel(RT));  // open: en
  Multiplexer #(.select(4), .width(16)) multiplexer_3 (
    .in0(_0_q), .in1(_1_q), .in2(_2_q), .in3(_3_q), .in4(_4_q), .in5(_5_q), .in6(_6_q), .in7(_7_q),
    .in8(_8_q), .in9(_9_q), .in10(_10_q), .in11(_11_q), .in12(_12_q), .in13(_13_q), .in14(_14_q),
    .in15(_15_q), .out(Output_RD), .sel(RD));  // open: en
endmodule

module Register_File (
);

  Register register_1 ();  // open: D, en, Q, clk, clr
  Register register_2 ();  // open: D, en, Q, clk, clr
  Register register_3 ();  // open: D, en, Q, clk, clr
endmodule
