// Logisim project alu-cpu copy.circ as structural Verilog
module Half (
  input  A,
  input  B,
  output Output,
  output Carry_Out
);

  wire and_1_out, not_1_out, or_1_out;

  and and_1 (and_1_out, A, B);
  or or_1 (or_1_out, A, B);
  and and_2 (Carry_Out, A, B);
  not not_1 (not_1_out, and_1_out);
  and and_3 (Output, not_1_out, or_1_out);
endmodule

module Full (
  input  A,
  input  B,
  input  Carry_In,
  output Carry_Out,
  output Output
);

  wire half_1_carry_out, half_1_output, half_2_carry_out;

  Half half_1 (.A(A), .B(B), .Output(half_1_output), .Carry_Out(half_1_carry_out));
  Half half_2 (.A(half_1_output), .B(Carry_In), .Output(Output), .Carry_Out(half_2_carry_out));
  or or_1 (Carry_Out, half_2_carry_out, half_1_carry_out);
endmodule

// ALU
module _16bits_ALU (
  input  [2:0] Op,
  input  [15:0] A,
  input  [15:0] B,
  output [15:0] Result,
  output Zero
);

  wire n4_binv_1_carry_out, n4_binv_3_carry_out, n4_binv_4_carry_out, or_1_out;

  _4_Binv u_4_binv_1 (
    .A(A[11:8]), .B(B[11:8]), .in_1(n4_binv_4_carry_out), .in_2(Op[2]), .in_3(Op[1:0]), .out_6(Result[11:8]),
    .Carry_Out(n4_binv_1_carry_out));
  _4_Binv u_4_binv_2 (
    .A(A[15:12]), .B(B[15:12]), .in_1(n4_binv_1_carry_out), .in_2(Op[2]), .in_3(Op[1:0]),
    .out_6(Result[15:12]));  // open: Carry_Out
  _4_Binv u_4_binv_3 (
    .A(A[3:0]), .B(B[3:0]), .in_1(Op[2]), .in_2(Op[2]), .in_3(Op[1:0]), .out_6(Result[3:0]),
    .Carry_Out(n4_binv_3_carry_out));
  _4_Binv u_4_binv_4 (
    .A(A[7:4]), .B(B[7:4]), .in_1(n4_binv_3_carry_out), .in_2(Op[2]), .in_3(Op[1:0]), .out_6(Result[7:4]),
    .Carry_Out(n4_binv_4_carry_out));
  or or_1 (or_1_out, Result[0], Result[1], Result[2], Result[3], Result[4], Result[5], Result[6], Result[7], Result[8], Result[9], Result[10], Result[11], Result[12], Result[13], Result[14], Result[15]);
  not not_1 (Zero, or_1_out);

  // Notes on the sheet:
  //   Bianca I. Colon Rosado // 801-13-1412 // ALU 16bits
  //   Op Code
  //   000 -> and
  //   001 -> or
  //   010 -> add
  //   011 -> not
  //   110 -> sub
  //   100 -> ldhi
endmodule

module And_or_Add (
  input  [1:0] in_1,
  input  Carry_In,
  input  A,
  input  B,
  output Output,
  output Carry_Out
);

  wire and_1_out, full_1_output, or_1_out;

  and and_1 (and_1_out, A, B);
  or or_1 (or_1_out, A, B);
  Full full_1 (.A(A), .B(B), .Carry_In(Carry_In), .Carry_Out(Carry_Out), .Output(full_1_output));
  Multiplexer #(.select(2), .enable("false")) multiplexer_1 (
    .in0(and_1_out), .in1(or_1_out), .in2(full_1_output), .out(Output), .sel(in_1));  // open: in3
endmodule

module Adder (
  input  Carry_In,
  input  A,
  input  B,
  output Carry_Out
);

  wire and_1_out, and_2_out, and_3_out;

  and and_1 (and_1_out, Carry_In, A);
  and and_2 (and_2_out, Carry_In, B);
  and and_3 (and_3_out, A, B);
  or or_1 (Carry_Out, and_1_out, and_2_out, and_3_out);
endmodule

module _2BitsALU (
  input  Carry_In,
  input  B_Inv,
  input  [1:0] Alu_OP,
  input  A,
  input  B,
  output Result,
  output Carry_Out
);

  wire and_1_out, full_1_output, multiplexer_1_out, not_1_out, not_2_out, Or_2_out, Or_out;

  Multiplexer #(.enable("false")) multiplexer_1 (.in0(B), .in1(not_1_out), .out(multiplexer_1_out), .sel(B_Inv));
  not not_1 (not_1_out, B);
  and and_1 (and_1_out, A, multiplexer_1_out);
  or Or (Or_out, A, multiplexer_1_out);
  Full full_1 (.A(A), .B(multiplexer_1_out), .Carry_In(Carry_In), .Carry_Out(Carry_Out), .Output(full_1_output));
  or Or_2 (Or_2_out, A, B);
  not not_2 (not_2_out, Or_2_out);
  Multiplexer #(.select(2), .enable("false")) multiplexer_2 (
    .in0(and_1_out), .in1(Or_out), .in2(full_1_output), .in3(not_2_out), .out(Result), .sel(Alu_OP));
endmodule

module Ainvert_5_9 (
  input  A_inv,
  input  B_inv,
  input  Carry_In,
  input  [1:0] in_4,
  input  A,
  input  B,
  input  Less,
  output Result,
  output Carry_Out
);

  wire and_1_out, full_1_output, multiplexer_1_out, multiplexer_2_out, not_1_out, not_2_out, or_1_out;

  Multiplexer #(.enable("false")) multiplexer_1 (.in0(A), .in1(not_1_out), .out(multiplexer_1_out), .sel(A_inv));
  not not_1 (not_1_out, A);
  not not_2 (not_2_out, B);
  Multiplexer #(.enable("false")) multiplexer_2 (.in0(B), .in1(not_2_out), .out(multiplexer_2_out), .sel(B_inv));
  and and_1 (and_1_out, multiplexer_1_out, multiplexer_2_out);
  or or_1 (or_1_out, multiplexer_1_out, multiplexer_2_out);
  Full full_1 (
    .A(multiplexer_1_out), .B(multiplexer_2_out), .Carry_In(Carry_In), .Carry_Out(Carry_Out),
    .Output(full_1_output));
  Multiplexer #(.select(2), .enable("false")) multiplexer_3 (
    .in0(and_1_out), .in1(or_1_out), .in2(full_1_output), .in3(Less), .out(Result), .sel(in_4));
endmodule

module _5_10 (
  input  Carry_In,
  input  [1:0] in_2,
  input  A_inv,
  input  B_inv,
  input  A,
  input  B,
  input  Less,
  output Result,
  output Carry_Out
);

  wire and_1_out, full_1_output, multiplexer_1_out, multiplexer_2_out, not_1_out, not_2_out, or_1_out;

  Multiplexer #(.enable("false")) multiplexer_1 (.in0(A), .in1(not_1_out), .out(multiplexer_1_out), .sel(A_inv));
  not not_1 (not_1_out, A);
  Multiplexer #(.enable("false")) multiplexer_2 (.in0(B), .in1(not_2_out), .out(multiplexer_2_out), .sel(B_inv));
  not not_2 (not_2_out, B);
  and and_1 (and_1_out, multiplexer_1_out, multiplexer_2_out);
  or or_1 (or_1_out, multiplexer_1_out, multiplexer_2_out);
  Full full_1 (
    .A(multiplexer_1_out), .B(multiplexer_2_out), .Carry_In(Carry_In), .Carry_Out(Carry_Out),
    .Output(full_1_output));
  Multiplexer #(.select(2), .enable("false")) multiplexer_3 (
    .in0(and_1_out), .in1(or_1_out), .in2(full_1_output), .in3(Less), .out(Result), .sel(in_2));

  // Notes on the sheet:
  //   ???
endmodule

// 4BitsALU
module _4_Binv (
  input  in_1,
  input  in_2,
  input  [1:0] in_3,
  input  [3:0] A,
  input  [3:0] B,
  output [3:0] out_6,
  output Carry_Out
);

  wire n2bitsalu_1_carry_out, n2bitsalu_2_carry_out, n2bitsalu_3_carry_out;

  _2BitsALU u_2bitsalu_1 (
    .A(A[0]), .B(B[0]), .Carry_In(in_1), .B_Inv(in_2), .Alu_OP(in_3), .Result(out_6[0]),
    .Carry_Out(n2bitsalu_1_carry_out));
  _2BitsALU u_2bitsalu_2 (
    .A(A[1]), .B(B[1]), .Carry_In(n2bitsalu_1_carry_out), .B_Inv(in_2), .Alu_OP(in_3), .Result(out_6[1]),
    .Carry_Out(n2bitsalu_2_carry_out));
  _2BitsALU u_2bitsalu_3 (
    .A(A[2]), .B(B[2]), .Carry_In(n2bitsalu_2_carry_out), .B_Inv(in_2), .Alu_OP(in_3), .Result(out_6[2]),
    .Carry_Out(n2bitsalu_3_carry_out));
  _2BitsALU u_2bitsalu_4 (
    .A(A[3]), .B(B[3]), .Carry_In(n2bitsalu_3_carry_out), .B_Inv(in_2), .Alu_OP(in_3), .Result(out_6[3]),
    .Carry_Out(Carry_Out));
endmodule
